# Fritzing sketch Saw2Sqr (saved by Fritzing 0.9.4)
breadboards: 1

parts:
  IC1 = Dual Op-Amp [package=dip08]
  R1 = Rotary Potentiometer (Small) [maximum_resistance=100kΩ package=THT]
  R2 = Resistor [tolerance=±5% resistance=68k package=THT]
  R3 = Rotary Potentiometer (Small) [maximum_resistance=100kΩ package=THT]
  R4 = Resistor [tolerance=±5% resistance=220k package=THT]
  R5 = Resistor [tolerance=±5% resistance=2.2M package=THT]
  R6 = Resistor [tolerance=±5% resistance=2.2k package=THT]
  R7 = Resistor [tolerance=±5% resistance=1.8k package=THT]
  C1 = Ceramic Capacitor [capacitance=100nF package="100 mil [THT, multilayer]"]
  C2 = Ceramic Capacitor [capacitance=100nF package="100 mil [THT, multilayer]"]
  C3 = Electrolytic Capacitor [capacitance=1µF package="100 mil [THT, electrolytic]"]
  C4 = Electrolytic Capacitor [capacitance=1µF package="100 mil [THT, electrolytic]"]

nets:
  N1: IC1.A_OUT, IC1.A_-IN, R3.leg1, R3.wiper, R3.leg2, R4.Pin_1
  N2: IC1.A_+IN, R1.wiper
  N3: IC1.A_V-, C2.0, C4.-
  N4: IC1.B_-IN, R4.Pin_0, R5.Pin_1
  N5: IC1.B_OUT, R6.Pin_1
  N6: IC1.A_V+, R2.Pin_0, C1.0, C3.+
  N7: R1.leg1, R5.Pin_0, R6.Pin_0, R7.Pin_0, R7.Pin_1, C1.1, C2.1, C3.-, C4.+
  N8: R1.leg2, R2.Pin_1

notes:
  OUT
  From
  SawVCO
  PWM
  PWM MOD
  50kA
  PWM
  50kB
  GND
  +12V
  -12V
  GND
